# Fritzing sketch OpenMQTTGateway ESP32 nRF24L01 BME280 IR (saved by Fritzing 0.9.3b)
perfboards: 1

parts:
  M1 = DOIT Esp32 DevKit v1 (30 pins long, 11 pins width) [part_number=ESP32S-PIN30]
  Part1 = GY-BMEP280 Barometric Pressure Sensor - Breakout
  C1 = Electrolytic Capacitor [capacitance=10µF voltage=16V package="100 mil [THT, electrolytic]"]
  Part2 = NRF24L01+ Breakout Board
  C2 = Ceramic Capacitor [capacitance=100nF package="100 mil [THT, multilayer]"]

nets:
  VCC: M1.3V3, Part1.VCC, C1.+, Part2.VCC, C2.1
  GND: M1.GND, Part1.GND, C1.-, Part2.GND, C2.0
  N1: M1.D4, Part2.IRQ
  N2: M1.D5, Part2.CS
  N3: M1.D18, Part2.SCK
  N4: M1.D19, Part2.MISO
  N5: M1.D21, Part1.SDA
  N6: M1.D22, Part1.SCL
  N7: M1.D23, Part2.MOSI
  N8: M1.D25, Part2.CE

custom parts:
  DOIT Esp32 DevKit v1 (30 pins long, 11 pins width): The DOIT Esp32 DevKit v1 is one of the development board created by DOIT to evaluate the ESP-WROOM-32 module. It is based on the ESP32 microcontroller that boasts Wifi, Bluetooth, Ethernet and Low Power support all in a single chip. (vanepp) made breadboard work, adjusted pin numbering and labels and reduced size of schematic and cleaned up pcb. This chip is 30pins long (2 x15) and 11 pins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
  GY-BMEP280 Barometric Pressure Sensor - Breakout: The BME280 is a chip which was originally designed for the next generation of smartphones. It is made up of a very accurate pressure sensor and an associated temperature sensor which helps calibrate the pressure readings. And just for fun they threw in a pretty solid humidity sensor in there as well! So with an I2C connection you have access to enough weather data to make some pretty good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
